# Fritzing sketch dpa-hall (saved by Fritzing 0.9.3b)
breadboards: 1

parts:
  JP1 = Header 10 [package=1x10-2mm-smd]
  3-pins_Hall_Effect_Sensor1 = mystery part, 3 pins [chip_label="Hall Effect Sensor"]

nets:
  N1: JP1.3, 3-pins_Hall_Effect_Sensor1.pin3
  N2: JP1.5, 3-pins_Hall_Effect_Sensor1.pin2
  N3: JP1.6, 3-pins_Hall_Effect_Sensor1.pin1

notes:
  IQRFBB-10
  EQ13 ->
  VO ->
  GND ->
  KS0020 Hall
  [I] [+] [S]
