# Fritzing sketch HTU21D (saved by Fritzing 0.9.3b)
breadboards: 1

parts:
  Part3 = HTU21D Breakout
  Part4 = Iqrf development board

nets:
  N1: Part3.SCL, Part4.A3
  N2: Part3.SDA, Part4.A2
  N3: Part3.GND, Part4.A4
  N4: Part3.3.3V, Part4.A5

custom parts:
  HTU21D Breakout: This is a breadboard friendly breakout board for the Measurement Specialties high-precision, low-power digital humidity sensor.
  Iqrf development board: Description: This is our board!!!
