# Fritzing sketch example-di (saved by Fritzing 0.9.3b)
breadboards: 1

parts:
  JP1 = Header 10 [package=1x10-2mm-smd]
  S1 = Pushbutton [package="[THT]"]

nets:
  N1: JP1.3, S1.Pin_3, S1.Pin_4
  N2: S1.Pin_1, S1.Pin_2

notes:
  IQRFBB-10
  EQ13 ->
  GND ->
