# Fritzing sketch example-standardPhotorezistor (saved by Fritzing 0.9.3b)
breadboards: 1

parts:
  JP1 = Header 10 [package=1x10-2mm-smd]
  R1 = Photocell (LDR) [package=THT]
  R2 = Resistor [tolerance=±5% resistance=10k package=THT]

nets:
  N1: JP1.4, R2.Pin_0
  N2: JP1.5, R1.pin_1
  N3: JP1.6, R1.pin_0, R2.Pin_1

notes:
  IQRFBB-10
  GRND ->
  VCC ->
  C1->
