# Fritzing sketch example-standardThermistor (saved by Fritzing 0.9.3b)
breadboards: 1

parts:
  JP1 = Header 10 [package=1x10-2mm-smd]
  T1 = LM35 Temperature Sensor [package="TO92 [THT]"]

nets:
  N1: JP1.4, T1.GND
  N2: JP1.5, T1.+Vs
  N3: JP1.6, T1.Vout

notes:
  IQRFBB-10
  GRND ->
  VCC ->
  C5->
