# Fritzing sketch example-do (saved by Fritzing 0.9.3b)
breadboards: 1

parts:
  JP1 = Header 10 [package=1x10-2mm-smd]
  R2 = Resistor [tolerance=±5% resistance=330 package=THT]
  LED1 = LED - 5mm [color="Red (633nm)" package="5 mm [THT]"]

nets:
  N1: JP1.3, LED1.cathode
  N2: JP1.4, R2.Pin_1
  N3: R2.Pin_0, LED1.anode

notes:
  IQRFBB-10
  SCL ->
  GND ->
