# Fritzing sketch example-ePir (saved by Fritzing 0.9.3b)
breadboards: 1

parts:
  JP1 = Header 10 [package=1x10-2mm-smd]
  U1 = Header 8 [package=1x08_smd]

nets:
  N1: JP1.4, U1.1, U1.3, U1.4, U1.8
  N2: JP1.5, U1.2, U1.6, U1.7
  N3: JP1.9, U1.5

notes:
  Grove ePIR pins:
  1, 2, 3,.. ..8
  IQRFBB-10
  GND ->
  VO ->
  EQ13 ->
